# Fritzing sketch Potencia (saved by Fritzing 0.9.4)

parts:
  POWER_SOURCE_12VDC = Power Source 12V 30W [package=sot23-5]
  POWER_SOURCE_24VDC = fuente
  L1 = sensor mono AC [package="400 mil [THT]"]  # not connected
  L2 = sensor mono AC [package="400 mil [THT]"]  # not connected
  AC1 = AC Power
  AC1_1 = AC Power  # not connected
  AC1_2 = AC Power  # not connected
  AC2 = AC Power
  AC2_1 = AC Power  # not connected
  AC2_2 = AC Power  # not connected
  MCU_en_modulo_iluminacion = DOIT Esp32 DevKit v1 (30 pins long, 11 pins width) [part_number=ESP32S-PIN30]  # not connected

nets:
  N1: POWER_SOURCE_12VDC.L, AC2.connector1
  N2: POWER_SOURCE_12VDC.N, AC2.connector0
  N3: POWER_SOURCE_24VDC.L, AC1.connector1
  N4: POWER_SOURCE_24VDC.N, AC1.connector0

notes:
  Salida 24Vdc
  Salida 12Vdc

custom parts:
  Power Source 12V 30W: Fuente de poder 12V 30W 2,5A
  fuente: fuente poder
  sensor mono AC: sensor Inductor corriente monofasica alterna
  AC Power: A generic ac power supply. (“Plug image: Freepik.com”. This project has been designed using resources from Freepik.com) ("Designed by macrovector / Freepik")
  AC Power: A generic ac power supply. (“Plug image: Freepik.com”. This project has been designed using resources from Freepik.com) ("Designed by macrovector / Freepik")
  AC Power: A generic ac power supply. (“Plug image: Freepik.com”. This project has been designed using resources from Freepik.com) ("Designed by macrovector / Freepik")
  DOIT Esp32 DevKit v1 (30 pins long, 11 pins width): The DOIT Esp32 DevKit v1 is one of the development board created by DOIT to evaluate the ESP-WROOM-32 module. It is based on the ESP32 microcontroller that boasts Wifi, Bluetooth, Ethernet and Low Power support all in a single chip. (vanepp) made breadboard work, adjusted pin numbering and labels and reduced size of schematic and cleaned up pcb. This chip is 30pins long (2 x15) and 11 pins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
