# Fritzing sketch iluminacion y ventilacion (saved by Fritzing 0.9.4)

parts:
  M1 = DOIT Esp32 DevKit v1 (30 pins long, 11 pins width) [part_number=ESP32S-PIN30]
  REGULADOR_A_5V = RioRand LM2596
  Current_and_Voltage_Sensor = MAX471 Current and Voltage Sensor Module
  TB1 = KF301-2 [part_number=KF301-2 package="screwterminal-5mm 2 position"]
  2_Channel_Relay = 2 Channel Power Relay
  SENSOR_AC_ILUMINACION = sensor mono AC [package="400 mil [THT]"]  # not connected
  SENSOR_AC_VENTILACION = sensor mono AC [package="400 mil [THT]"]  # not connected
  220VAC_OUT_ILUMINACION = AC Power female
  220VAC_OUT_ILUMINACION_1 = AC Power female  # not connected
  220VAC_OUT_ILUMINACION_2 = AC Power female  # not connected
  220VAC_OUT_VENTILACION = AC Power female
  220VAC_OUT_VENTILACION_1 = AC Power female  # not connected
  220VAC_OUT_VENTILACION_2 = AC Power female  # not connected
  220VAC_IN = AC Power
  220VAC_IN_1 = AC Power  # not connected
  220VAC_IN_2 = AC Power  # not connected
  SENSOR_AC_FUENTE_12V = sensor mono AC [package="400 mil [THT]"]  # not connected
  SENSOR_AC_FUENTE_24V = sensor mono AC [package="400 mil [THT]"]  # not connected

nets:
  N1: M1.GND, REGULADOR_A_5V.Pin_4, Current_and_Voltage_Sensor.GND#13
  N2: M1.VP, Current_and_Voltage_Sensor.VT
  N3: M1.VN, Current_and_Voltage_Sensor.AT
  N4: M1.D32, 2_Channel_Relay.IN1
  N5: M1.D33, 2_Channel_Relay.IN2
  VIN: M1.VIN, REGULADOR_A_5V.Pin_3, 2_Channel_Relay.VCC
  N6: REGULADOR_A_5V.Pin_1, Current_and_Voltage_Sensor.VOUT
  N7: REGULADOR_A_5V.Pin_2, Current_and_Voltage_Sensor.GND#8
  N8: Current_and_Voltage_Sensor.GND#10, TB1.1
  N9: Current_and_Voltage_Sensor.VIN, TB1.2
  N10: Current_and_Voltage_Sensor.GND#12, 2_Channel_Relay.GND
  N11: 2_Channel_Relay.K1-COM, 2_Channel_Relay.K2-COM, 220VAC_IN.connector0
  N12: 2_Channel_Relay.K1-NO, 220VAC_OUT_ILUMINACION.connector1
  N13: 2_Channel_Relay.K2-NO, 220VAC_OUT_VENTILACION.connector1

notes:
  ALIMENTACION 12VDC

custom parts:
  DOIT Esp32 DevKit v1 (30 pins long, 11 pins width): The DOIT Esp32 DevKit v1 is one of the development board created by DOIT to evaluate the ESP-WROOM-32 module. It is based on the ESP32 microcontroller that boasts Wifi, Bluetooth, Ethernet and Low Power support all in a single chip. (vanepp) made breadboard work, adjusted pin numbering and labels and reduced size of schematic and cleaned up pcb. This chip is 30pins long (2 x15) and 11 pins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
  MAX471 Current and Voltage Sensor Module: The MAX471 current and voltage sensor module is a bidirectional, highside current-sense amplifier. The current measurement maximum is 3 amps and the voltage measurement range is 3 to 25 volts. The operating voltage range is 3 to 36 volts.
  KF301-2: KF301-3 is a 3 position screw terminal header block with male through hole PCB pins on 5mm spacing
  2 Channel Power Relay: A 2 channel power relay. The module operates at 5V.
  sensor mono AC: sensor Inductor corriente monofasica alterna
  AC Power female: A generic ac power supply. (“Plug image: Freepik.com”. This project has been designed using resources from Freepik.com) ("Designed by macrovector / Freepik")
  AC Power female: A generic ac power supply. (“Plug image: Freepik.com”. This project has been designed using resources from Freepik.com) ("Designed by macrovector / Freepik")
  AC Power female: A generic ac power supply. (“Plug image: Freepik.com”. This project has been designed using resources from Freepik.com) ("Designed by macrovector / Freepik")
  AC Power: A generic ac power supply. (“Plug image: Freepik.com”. This project has been designed using resources from Freepik.com) ("Designed by macrovector / Freepik")
  AC Power: A generic ac power supply. (“Plug image: Freepik.com”. This project has been designed using resources from Freepik.com) ("Designed by macrovector / Freepik")
  AC Power: A generic ac power supply. (“Plug image: Freepik.com”. This project has been designed using resources from Freepik.com) ("Designed by macrovector / Freepik")
