# Fritzing sketch modulo riego (saved by Fritzing 0.9.4)

parts:
  Componente1 = LCD1602-I2C
  M1 = DOIT Esp32 DevKit v1 (30 pins long, 11 pins width) [part_number=ESP32S-PIN30]
  Arduino_Nano = Arduino Nano (Rev3.0)
  Current_and_Voltage_Sensor1 = MAX471 Current and Voltage Sensor Module
  Current_and_Voltage_Sensor_Bomba = MAX471 Current and Voltage Sensor Module
  24Vdc_IN = KF301-2 [part_number=KF301-2 package="screwterminal-5mm 2 position"]
  TB2 = KF301-2 [part_number=KF301-2 package="screwterminal-5mm 2 position"]
  12Vdc_IN = KF301-2 [part_number=KF301-2 package="screwterminal-5mm 2 position"]
  4_Channel_Relay_with_mod = 4 Channel Power Relay
  12Vdc_max_OUT_Bomba = KF301-2 [part_number=KF301-2 package="screwterminal-5mm 2 position"]
  Regulador_Vdc_Bomba = RioRand LM2596
  Componente3 = Si7021
  regulador_24Vdc/5Vdc = RioRand LM2596
  sensor_analogo_de_PH_y_termperatura_fogger = sensor PH
  Sensor_T°_H2O_fogger = DS18B20 1-Wire Temperature Sensor Probe Cable
  sensor_analogo_de_PH_y_termperatura_Spray = sensor PH
  Sensor_T°_H2O_Spray = DS18B20 1-Wire Temperature Sensor Probe Cable
  T°_y_H°_aéreo = DHT11 module
  Fogger_2 = Fogger  # not connected
  Fogger_1 = Fogger  # not connected
  Sensor_Flujo_Bomba = YF-S201 Water Flow Meter
  JACK1 = 2.1mm Barrel Jack with Terminal Block
  JACK2 = 2.1mm Barrel Jack with Terminal Block

nets:
  GND: Componente1.GND, M1.GND, Arduino_Nano.GND, Current_and_Voltage_Sensor_Bomba.GND#12, Current_and_Voltage_Sensor_Bomba.GND#13, 4_Channel_Relay_with_mod.GND, Componente3.GND, regulador_24Vdc/5Vdc.Pin_4, sensor_analogo_de_PH_y_termperatura_Spray.GND, Sensor_T°_H2O_Spray.GND, T°_y_H°_aéreo.GND, Sensor_Flujo_Bomba.GND
  VCC: Componente1.VCC, M1.VIN, Arduino_Nano.VIN, 4_Channel_Relay_with_mod.VCC, Componente3.VCC, regulador_24Vdc/5Vdc.Pin_3, sensor_analogo_de_PH_y_termperatura_fogger.Vin, Sensor_T°_H2O_fogger.VDD, sensor_analogo_de_PH_y_termperatura_Spray.Vin, Sensor_T°_H2O_Spray.VDD, T°_y_H°_aéreo.VCC, Sensor_Flujo_Bomba.VCC
  N1: Componente1.SDA, M1.D21, Componente3.SDA
  N2: Componente1.SCL, M1.D22, Componente3.SCL
  N3: M1.D4, Sensor_T°_H2O_fogger.DQ
  N4: M1.RX2, Arduino_Nano.D1/TX
  N5: M1.D19, 4_Channel_Relay_with_mod.IN4
  N6: M1.RX0, 4_Channel_Relay_with_mod.IN3
  N7: M1.TX0, 4_Channel_Relay_with_mod.IN2
  N8: M1.D23, 4_Channel_Relay_with_mod.IN1
  N9: M1.VP, Current_and_Voltage_Sensor1.VT
  N10: M1.VN, Current_and_Voltage_Sensor1.AT
  N11: M1.D34, Current_and_Voltage_Sensor_Bomba.AT
  N12: M1.D35, Current_and_Voltage_Sensor_Bomba.VT
  N13: M1.D32, T°_y_H°_aéreo.DATA
  N14: Arduino_Nano.D2, Sensor_T°_H2O_Spray.DQ
  N15: Arduino_Nano.A7, sensor_analogo_de_PH_y_termperatura_fogger.To
  N16: Arduino_Nano.A6, sensor_analogo_de_PH_y_termperatura_fogger.Po
  N17: Arduino_Nano.A2, Sensor_Flujo_Bomba.SIG
  N18: Arduino_Nano.A1, sensor_analogo_de_PH_y_termperatura_Spray.To
  N19: Arduino_Nano.A0, sensor_analogo_de_PH_y_termperatura_Spray.Po
  N20: Current_and_Voltage_Sensor1.GND#8, TB2.2, regulador_24Vdc/5Vdc.Pin_2, JACK1.NEG, JACK2.NEG
  N21: Current_and_Voltage_Sensor1.VOUT, TB2.1, 4_Channel_Relay_with_mod.COM#17, 4_Channel_Relay_with_mod.COM#20, regulador_24Vdc/5Vdc.Pin_1
  N22: Current_and_Voltage_Sensor1.GND#10, 24Vdc_IN.2
  N23: Current_and_Voltage_Sensor1.VIN, 24Vdc_IN.1
  GND_2: Current_and_Voltage_Sensor1.GND#12, Current_and_Voltage_Sensor1.GND#13, sensor_analogo_de_PH_y_termperatura_fogger.GND, Sensor_T°_H2O_fogger.GND
  N24: Current_and_Voltage_Sensor_Bomba.GND#8, 12Vdc_max_OUT_Bomba.2
  N25: Current_and_Voltage_Sensor_Bomba.VOUT, 12Vdc_max_OUT_Bomba.1
  N26: Current_and_Voltage_Sensor_Bomba.GND#10, Regulador_Vdc_Bomba.Pin_4
  N27: Current_and_Voltage_Sensor_Bomba.VIN, Regulador_Vdc_Bomba.Pin_3
  N28: 12Vdc_IN.1, Regulador_Vdc_Bomba.Pin_2
  N29: 12Vdc_IN.2, 4_Channel_Relay_with_mod.COM#23
  N30: 4_Channel_Relay_with_mod.NO#18, JACK2.POS
  N31: 4_Channel_Relay_with_mod.NO#21, JACK1.POS
  N32: 4_Channel_Relay_with_mod.NO#24, Regulador_Vdc_Bomba.Pin_1

custom parts:
  LCD1602-I2C: A standard character display, usually with 2x16 characters. Comes in many colors with LCM1602 IIC attached.
  DOIT Esp32 DevKit v1 (30 pins long, 11 pins width): The DOIT Esp32 DevKit v1 is one of the development board created by DOIT to evaluate the ESP-WROOM-32 module. It is based on the ESP32 microcontroller that boasts Wifi, Bluetooth, Ethernet and Low Power support all in a single chip. (vanepp) made breadboard work, adjusted pin numbering and labels and reduced size of schematic and cleaned up pcb. This chip is 30pins long (2 x15) and 11 pins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
  MAX471 Current and Voltage Sensor Module: The MAX471 current and voltage sensor module is a bidirectional, highside current-sense amplifier. The current measurement maximum is 3 amps and the voltage measurement range is 3 to 25 volts. The operating voltage range is 3 to 36 volts.
  KF301-2: KF301-3 is a 3 position screw terminal header block with male through hole PCB pins on 5mm spacing
  4 Channel Power Relay: A 4 channel power relay. The module operates at 5V.
  Si7021: Si7021 humidity and temperature sensor
  DHT11 module: DHT11 black pcb module
  Fogger: Piezo
  YF-S201 Water Flow Meter: The YF-S201 Flow Meter. The input voltage is 5V to 24V (DC).
