# Fritzing sketch ventilacion y temperatura (saved by Fritzing 0.9.4)

parts:
  M1 = DOIT Esp32 DevKit v1 (30 pins long, 11 pins width) [part_number=ESP32S-PIN30]
  Current_and_Voltage_Sensor = MAX471 Current and Voltage Sensor Module
  REGULADOR_24Vdc_a_12Vdc = RioRand LM2596
  REGULADOR_24Vdc_a_5Vdc = RioRand LM2596
  24V = KF301-2 [part_number=KF301-2 package="screwterminal-5mm 2 position"]
  LCD = LCD1602-I2C
  4_Channel_Relay = 4 Channel Power Relay
  SENSOR_T°_Y_H°_superior_foco = DHT11 module
  SENSOR_T°_Y_H°_inferior_foco = DHT11 module
  SENSOR_T°_Y_H°_interior_foco = DHT11 module
  VENTILADOR_INDUCTOR_FOCO = Fan - Ventilador [package=THT]
  VENTILADOR_EXTRACTOR_FOCO = Fan - Ventilador [package=THT]
  LED2 = LEDs [package=led10mm]  # not connected
  SENSOR_T°_Y_H°_modulo = Si7021

nets:
  VCC: M1.3V3, SENSOR_T°_Y_H°_superior_foco.VCC, SENSOR_T°_Y_H°_inferior_foco.VCC, SENSOR_T°_Y_H°_interior_foco.VCC
  GND: M1.GND, Current_and_Voltage_Sensor.GND#12, Current_and_Voltage_Sensor.GND#13, REGULADOR_24Vdc_a_5Vdc.Pin_4, LCD.GND, 4_Channel_Relay.GND, SENSOR_T°_Y_H°_superior_foco.GND, SENSOR_T°_Y_H°_inferior_foco.GND, SENSOR_T°_Y_H°_interior_foco.GND, SENSOR_T°_Y_H°_modulo.GND
  N1: M1.D15, SENSOR_T°_Y_H°_interior_foco.DATA
  N2: M1.TX2, 4_Channel_Relay.IN1
  N3: M1.D5, 4_Channel_Relay.IN2
  N4: M1.D18, 4_Channel_Relay.IN3
  N5: M1.D19, 4_Channel_Relay.IN4
  N6: M1.D21, LCD.SDA, SENSOR_T°_Y_H°_modulo.SDA
  N7: M1.D22, LCD.SCL, SENSOR_T°_Y_H°_modulo.SCL
  N8: M1.VP, Current_and_Voltage_Sensor.VT
  N9: M1.VN, Current_and_Voltage_Sensor.AT
  N10: M1.D34, SENSOR_T°_Y_H°_inferior_foco.DATA
  N11: M1.D35, SENSOR_T°_Y_H°_superior_foco.DATA
  VCC_2: M1.VIN, REGULADOR_24Vdc_a_5Vdc.Pin_3, LCD.VCC, 4_Channel_Relay.VCC, SENSOR_T°_Y_H°_modulo.VCC
  N12: Current_and_Voltage_Sensor.GND#8, REGULADOR_24Vdc_a_12Vdc.Pin_2, REGULADOR_24Vdc_a_5Vdc.Pin_2
  N13: Current_and_Voltage_Sensor.VOUT, REGULADOR_24Vdc_a_12Vdc.Pin_1, REGULADOR_24Vdc_a_5Vdc.Pin_1, 4_Channel_Relay.COM#23, 4_Channel_Relay.COM#26
  N14: Current_and_Voltage_Sensor.GND#10, 24V.2
  N15: Current_and_Voltage_Sensor.VIN, 24V.1
  N16: REGULADOR_24Vdc_a_12Vdc.Pin_3, 4_Channel_Relay.COM#17, 4_Channel_Relay.COM#20
  GND_2: REGULADOR_24Vdc_a_12Vdc.Pin_4, VENTILADOR_INDUCTOR_FOCO.GND, VENTILADOR_EXTRACTOR_FOCO.GND
  N17: 4_Channel_Relay.NO#18, 4_Channel_Relay.NO#27, VENTILADOR_EXTRACTOR_FOCO.5V
  N18: 4_Channel_Relay.NO#21, 4_Channel_Relay.NO#24, VENTILADOR_INDUCTOR_FOCO.5V

notes:
  ALIMENTACION 24VDC

custom parts:
  DOIT Esp32 DevKit v1 (30 pins long, 11 pins width): The DOIT Esp32 DevKit v1 is one of the development board created by DOIT to evaluate the ESP-WROOM-32 module. It is based on the ESP32 microcontroller that boasts Wifi, Bluetooth, Ethernet and Low Power support all in a single chip. (vanepp) made breadboard work, adjusted pin numbering and labels and reduced size of schematic and cleaned up pcb. This chip is 30pins long (2 x15) and 11 pins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
  MAX471 Current and Voltage Sensor Module: The MAX471 current and voltage sensor module is a bidirectional, highside current-sense amplifier. The current measurement maximum is 3 amps and the voltage measurement range is 3 to 25 volts. The operating voltage range is 3 to 36 volts.
  KF301-2: KF301-3 is a 3 position screw terminal header block with male through hole PCB pins on 5mm spacing
  LCD1602-I2C: A standard character display, usually with 2x16 characters. Comes in many colors with LCM1602 IIC attached.
  4 Channel Power Relay: A 4 channel power relay. The module operates at 5V.
  DHT11 module: DHT11 black pcb module
  Fan - Ventilador: Ventilador de 2 pines, se encuentra comunmente en computadoras de escritorio
  LEDs: LEDs Standard schematic elements and footprints for 5mm, 3mm, 1206, and 0603 sized LEDs. 5mm - Spark Fun Electronics SKU : COM-00529 (and others)
  Si7021: Si7021 humidity and temperature sensor
